// Logisim project Problema38.circ as structural Verilog
module BOARD_BIG_ASM (
  output out_1
);

  wire button_1_out, CLK, CLR, d_ff_1_q, not_1_out, Write, Write_ASCII;
  wire [6:0] ASCII;
  wire [7:0] counter_1_q;
  wire [23:0] Dir_INPUT, Dir_MEMORY;
  wire [31:0] INPUT, MEMORY_IN, MEMORY_OUT;

  Button button_1 (.out(button_1_out));
  Clock clock_1 (.out(CLK));
  D_Flip_Flop d_ff_1 (.clk(CLK), .D(1'b1), .Q(d_ff_1_q), .reset(button_1_out));  // open: Qn, preset, en
  D_Flip_Flop d_ff_2 (.clk(CLK), .D(d_ff_1_q), .Qn(CLR), .reset(button_1_out));  // open: Q, preset, en
  BIG_ASM big_asm_1 (
    .DATA_INPUT(INPUT), .MEMORY_IN(MEMORY_OUT), .CLK(CLK), .CLR(CLR), .DIR_INPUT(Dir_INPUT),
    .MEMORY_OUT(MEMORY_IN), .DIR_MEMORY(Dir_MEMORY), .Write_OUTPUT(Write), .ASCII(ASCII),
    .Write_ASCII(Write_ASCII), .END(out_1));
  MEMORY memory_1 (.DIR(Dir_MEMORY), .DATA_IN(MEMORY_IN), .WRITE(Write), .CLK(CLK), .CLR(CLR), .DATA_OUT(MEMORY_OUT));
  INPUT input_1 (.DIR(Dir_INPUT), .CLK(CLK), .DATA_OUT(INPUT));
  Counter counter_1 (.load(1'b0), .count(not_1_out), .Q(counter_1_q), .clk(CLK), .clr(CLR));  // open: D, carry
  not not_1 (not_1_out, out_1);
  // Probe on counter_1_q
  TTY #(.rows(32), .cols(60)) tty_1 (.data(ASCII), .clk(CLK), .we(Write_ASCII), .clr(CLR));

  // Other names for the same wires on the sheet: END = out_1

  // Notes on the sheet:
  //   COUNTER
  //   BOARD
endmodule

module INPUT (
  input  [23:0] DIR,
  input  CLK,
  output [31:0] DATA_OUT
);

  RAM #(.addrWidth(24), .dataWidth(32)) ram_1 (.addr(DIR), .data(DATA_OUT), .clk(CLK), .ld(1'b1));  // open: sel, clr
endmodule

module MEMORY (
  input  [23:0] DIR,
  input  [31:0] DATA_IN,
  input  WRITE,
  input  CLK,
  input  CLR,
  output [31:0] DATA_OUT
);

  wire not_1_out;

  not not_1 (not_1_out, WRITE);
  RAM #(.addrWidth(24), .dataWidth(32), .bus("separate")) ram_1 (
    .addr(DIR), .din(DATA_IN), .data(DATA_OUT), .clk(CLK), .ld(not_1_out), .clr(CLR));  // open: str, sel
endmodule

module BIG_ASM (
  input  [31:0] DATA_INPUT,
  input  [31:0] MEMORY_IN,
  input  CLK,
  input  CLR,
  output [23:0] DIR_INPUT,
  output [31:0] MEMORY_OUT,
  output [23:0] DIR_MEMORY,
  output Write_OUTPUT,
  output [6:0] ASCII,
  output Write_ASCII,
  output END
);

  wire C__1, C__2, C____Na, LC1, LC2, LN, LNa, LW1, LW2, NEWLINE1, NEWLINE2, NEWLINE3, Start, W___N, WAIT_q,
       Write1, Write2, Write_END;

  D_Flip_Flop WAIT (.clk(CLK), .D(1'b0), .Q(WAIT_q), .preset(CLR));  // open: Qn, en, reset
  D_Flip_Flop WAIT_2 (.clk(CLK), .D(WAIT_q), .Q(Start), .reset(CLR));  // open: Qn, preset, en
  DATA_PATH data_path_1 (
    .CLK(CLK), .CLR(CLR), .DATA_INPUT(DATA_INPUT), .LNa(LNa), .LN(LN), .LW1(LW1), .LC1(LC1), .C__1(C__1),
    .Write1(Write1), .NEWLINE1(NEWLINE1), .DIR_INPUT(DIR_INPUT), .C____Na(C____Na), .W___N(W___N),
    .ASCII(ASCII), .WASCII(Write_ASCII), .WriteEND(Write_END), .LC2(LC2), .C__2(C__2), .LW2(LW2),
    .Write2(Write2), .NEWLINE2(NEWLINE2), .NEWLINE3(NEWLINE3));
  CONTROL_UNIT control_unit_1 (
    .CLK(CLK), .C____Na(C____Na), .W___N(W___N), .CLR(CLR), .Start(Start), .LNa(LNa), .LN(LN), .LC1(LC1),
    .LW1(LW1), .Write1(Write1), .NEWLINE1(NEWLINE1), .C__1(C__1), .END(END), .WriteEnd(Write_END), .LC2(LC2),
    .LW2(LW2), .C__2(C__2), .Write2(Write2), .NEWLINE2(NEWLINE2), .NEWLINE3(NEWLINE3));
endmodule

module PRINT_UDEC (
  input  [31:0] num,
  input  start,
  input  CLK,
  input  RST,
  output [6:0] ASCII,
  output Write_ASCII,
  output \end 
);

  wire _0_c, _0_n, demultiplexer_1_out0, demultiplexer_2_out0, demultiplexer_2_out1, demultiplexer_3_out0,
       demultiplexer_3_out1, IDLE_2_q, IDLE_3_q, IDLE_4_q, IDLE_q, Lc, Lc_0, Ln, Ln_0, or_1_out;
  wire [23:0] bit_extender_1_out;
  wire [31:0] c, c___1, c___1_t, divider_1_rem, memory_1_data_out, multiplexer_1_out, multiplexer_2_out,
       multiplexer_3_out, n, n___10, n___10___48;

  Multiplexer #(.width(32), .enable("false")) multiplexer_1 (
    .in0(num), .in1(n___10), .out(multiplexer_1_out), .sel(Lc_0));
  Divider #(.width(32)) divider_1 (.a(n), .b(32'ha), .out(n___10), .rem(divider_1_rem));  // open: upper
  Adder #(.width(32)) adder_1 (.a(divider_1_rem), .b(32'h30), .out(n___10___48));  // open: cin, cout
  or or_1 (or_1_out, demultiplexer_1_out0, \end );
  Register #(.width(32)) u_n (.D(multiplexer_1_out), .en(Ln), .Q(n), .clk(CLK), .clr(RST));
  D_Flip_Flop IDLE (.clk(CLK), .D(or_1_out), .Q(IDLE_q), .preset(RST));  // open: Qn, en, reset
  Demultiplexer #(.enable("false")) demultiplexer_1 (
    .out0(demultiplexer_1_out0), .out1(Ln_0), .in(IDLE_q), .sel(start));
  or or_2 (Write_ASCII, demultiplexer_3_out0, demultiplexer_2_out1);
  Multiplexer #(.width(32), .enable("false")) multiplexer_2 (
    .in0(c___1), .in1(c___1_t), .out(multiplexer_2_out), .sel(Write_ASCII));
  Adder #(.width(32)) adder_2 (.a(c), .b(32'h1), .out(c___1));  // open: cin, cout
  Subtractor #(.width(32)) subtractor_1 (.a(c), .b(32'h1), .out(c___1_t));  // open: bin, bout
  D_Flip_Flop IDLE_2 (.clk(CLK), .D(Ln_0), .Q(IDLE_2_q), .reset(RST));  // open: Qn, preset, en
  Register #(.width(32)) u_c (.D(multiplexer_2_out), .en(Lc), .Q(c), .clk(CLK), .clr(RST));
  or or_3 (Lc_0, IDLE_2_q, demultiplexer_3_out1);
  Multiplexer #(.width(32), .enable("false")) multiplexer_3 (
    .in0(c), .in1(c___1_t), .out(multiplexer_3_out), .sel(Write_ASCII));
  Comparator #(.width(32), .mode("unsigned")) comparator_1 (.a({32{1'b0}}), .b(n), .lt(_0_n));  // open: gt, eq
  Comparator #(.width(32), .mode("unsigned")) comparator_2 (.a({32{1'b0}}), .b(c), .lt(_0_c));  // open: gt, eq
  D_Flip_Flop IDLE_3 (.clk(CLK), .D(Write_ASCII), .Q(IDLE_3_q), .reset(RST));  // open: Qn, preset, en
  Demultiplexer #(.enable("false")) demultiplexer_2 (
    .out0(demultiplexer_2_out0), .out1(demultiplexer_2_out1), .in(IDLE_3_q), .sel(_0_c));
  Bit_Extender #(.in_width(32), .out_width(24)) bit_extender_1 (.in(multiplexer_3_out), .out(bit_extender_1_out));
  D_Flip_Flop IDLE_4 (.clk(CLK), .D(Lc_0), .Q(IDLE_4_q), .reset(RST));  // open: Qn, preset, en
  or or_4 (Lc, Lc_0, Write_ASCII);
  or or_5 (Ln, Ln_0, Lc_0);
  Demultiplexer #(.enable("false")) demultiplexer_3 (
    .out0(demultiplexer_3_out0), .out1(demultiplexer_3_out1), .in(IDLE_4_q), .sel(_0_n));
  D_Flip_Flop IDLE_5 (.clk(CLK), .D(demultiplexer_2_out0), .Q(\end ), .reset(RST));  // open: Qn, preset, en
  MEMORY memory_1 (
    .DIR(bit_extender_1_out), .DATA_IN(n___10___48), .WRITE(Lc_0), .CLK(CLK), .CLR(RST),
    .DATA_OUT(memory_1_data_out));
  Bit_Extender #(.in_width(32), .out_width(7)) bit_extender_2 (.in(memory_1_data_out), .out(ASCII));

  // Other names for the same wires on the sheet: Lc_1 = Write_ASCII; Sc = Write_ASCII; Ln_1 = Lc_0; Sn = Lc_0;
  //   Write = Lc_0
endmodule

module PRINT_DEC (
  input  [31:0] num,
  input  start,
  input  CLK,
  input  RST,
  output [6:0] ASCII,
  output Write_ASCII,
  output END
);

  wire demultiplexer_1_out0, demultiplexer_1_out1, demultiplexer_2_out0, demultiplexer_3_out0, end_t,
       IDLE_3_q, IDLE_q, or_1_out, or_2_out, or_3_out, S_ASCII, startUDEC, Write_ASCII_1;
  wire [6:0] ASCII_t;
  wire [31:0] multiplexer_1_out, negator_1_out;

  or or_1 (or_1_out, demultiplexer_1_out0, END);
  Negator #(.width(32)) negator_1 (.in(num), .out(negator_1_out));
  D_Flip_Flop IDLE (.clk(CLK), .D(or_1_out), .Q(IDLE_q), .preset(RST));  // open: Qn, en, reset
  Demultiplexer #(.enable("false")) demultiplexer_1 (
    .out0(demultiplexer_1_out0), .out1(demultiplexer_1_out1), .in(IDLE_q), .sel(start));
  Multiplexer #(.width(32), .enable("false")) multiplexer_1 (
    .in0(num), .in1(negator_1_out), .out(multiplexer_1_out), .sel(num[31]));
  Demultiplexer #(.enable("false")) demultiplexer_2 (
    .out0(demultiplexer_2_out0), .out1(S_ASCII), .in(demultiplexer_1_out1), .sel(num[31]));
  or or_2 (or_2_out, demultiplexer_2_out0, S_ASCII);
  D_Flip_Flop IDLE_2 (.clk(CLK), .D(or_2_out), .Q(startUDEC), .reset(RST));  // open: Qn, preset, en
  PRINT_UDEC print_udec_1 (
    .num(multiplexer_1_out), .start(startUDEC), .CLK(CLK), .RST(RST), .ASCII(ASCII_t),
    .Write_ASCII(Write_ASCII_1), .\end (end_t));
  D_Flip_Flop IDLE_3 (.clk(CLK), .D(or_3_out), .Q(IDLE_3_q), .reset(RST));  // open: Qn, preset, en
  or or_3 (or_3_out, startUDEC, demultiplexer_3_out0);
  Demultiplexer #(.enable("false")) demultiplexer_3 (
    .out0(demultiplexer_3_out0), .out1(END), .in(IDLE_3_q), .sel(end_t));
  Multiplexer #(.width(7), .enable("false")) multiplexer_2 (
    .in0(ASCII_t), .in1(7'b0101101), .out(ASCII), .sel(S_ASCII));
  or or_4 (Write_ASCII, S_ASCII, Write_ASCII_1);

  // Other names for the same wires on the sheet: sign = num[31]; Write_ASCII_0 = S_ASCII
endmodule

module TEST_PRINT (
  input  [31:0] in_1,
  output out_2
);

  wire button_1_out, button_2_out, CLK, CLR, d_ff_1_q, Write_ASCII;
  wire [6:0] ASCII;

  Button button_1 (.out(button_1_out));
  Clock clock_1 (.out(CLK));
  D_Flip_Flop d_ff_1 (.clk(CLK), .D(1'b1), .Q(d_ff_1_q), .reset(button_1_out));  // open: Qn, preset, en
  D_Flip_Flop d_ff_2 (.clk(CLK), .D(d_ff_1_q), .Qn(CLR), .reset(button_1_out));  // open: Q, preset, en
  Button button_2 (.out(button_2_out));
  PRINT_UDEC print_udec_1 ();  // open: num, start, CLK, RST, ASCII, Write_ASCII, end
  PRINT_DEC print_dec_1 (
    .num(in_1), .start(button_2_out), .CLK(CLK), .RST(CLR), .ASCII(ASCII), .Write_ASCII(Write_ASCII),
    .END(out_2));
  TTY #(.rows(32), .cols(60)) tty_1 (.data(ASCII), .clk(CLK), .we(Write_ASCII), .clr(CLR));
endmodule

module DATA_PATH (
  input  CLK,
  input  CLR,
  input  [31:0] DATA_INPUT,
  input  LNa,
  input  LN,
  input  LW1,
  input  LW2,
  input  LC1,
  input  LC2,
  input  C__1,
  input  C__2,
  input  Write1,
  input  Write2,
  input  NEWLINE1,
  input  NEWLINE2,
  input  NEWLINE3,
  output [23:0] DIR_INPUT,
  output C____Na,
  output [6:0] ASCII,
  output W___N,
  output WriteEND,
  output WASCII
);

  wire C_plus_plus, comparator_1_eq, comparator_1_lt, LC, LW, NEWLINE, or_3_out, or_8_out,
       print_udec_1_write_ascii, WAIT_q, Write;
  wire [6:0] print_udec_1_ascii;
  wire [23:0] adder_2_out, multiplexer_2_out, multiplexer_3_out;
  wire [31:0] adder_1_out, C, divider_1_rem, INC, N, Na, W;

  Adder #(.width(32)) adder_1 (.a(C), .b(32'h1), .out(adder_1_out));  // open: cin, cout
  or or_1 (LC, LC1, LC2);
  or or_2 (C_plus_plus, C__1, C__2);
  or or_3 (or_3_out, LC, C_plus_plus);
  Multiplexer #(.width(32), .enable("false")) multiplexer_1 (
    .in0(32'h1), .in1(adder_1_out), .out(INC), .sel(C_plus_plus));
  Comparator #(.width(32), .mode("unsigned")) comparator_1 (
    .a(C), .b(Na), .eq(comparator_1_eq), .lt(comparator_1_lt));  // open: gt
  Divider #(.width(32)) divider_1 (.a(N), .b(W), .rem(divider_1_rem));  // open: out, upper
  Comparator #(.width(32), .mode("unsigned")) comparator_2 (
    .a(divider_1_rem), .b({32{1'b0}}), .eq(W___N));  // open: gt, lt
  // Probe on Na
  Register #(.width(32)) u_Na (.D(DATA_INPUT), .en(LNa), .Q(Na), .clk(CLK), .clr(CLR));
  // Probe on C
  Register #(.width(32)) u_C (.D(INC), .en(or_3_out), .Q(C), .clk(CLK), .clr(CLR));
  or or_4 (C____Na, comparator_1_eq, comparator_1_lt);
  or or_5 (LW, LW1, LW2);
  or or_6 (Write, Write1, Write2);
  Multiplexer #(.width(24), .enable("false")) multiplexer_2 (
    .in1(C[23:0]), .out(multiplexer_2_out), .sel(LW));  // open: in0
  Register #(.width(32)) u_N (.D(DATA_INPUT), .en(LN), .Q(N), .clk(CLK), .clr(CLR));
  Register #(.width(32)) u_W (.D(DATA_INPUT), .en(LW), .Q(W), .clk(CLK), .clr(CLR));
  // Probe on N
  // Probe on W
  Multiplexer #(.width(24), .enable("false")) multiplexer_3 (
    .in0(multiplexer_2_out), .in1(adder_2_out), .out(multiplexer_3_out), .sel(LN));
  Adder #(.width(24)) adder_2 (.a(Na[23:0]), .b(24'h1), .out(adder_2_out));  // open: cin, cout
  or or_7 (NEWLINE, NEWLINE1, NEWLINE2, NEWLINE3);
  PRINT_UDEC print_udec_1 (
    .num(W), .start(Write), .CLK(CLK), .RST(CLR), .ASCII(print_udec_1_ascii),
    .Write_ASCII(print_udec_1_write_ascii), .\end (WriteEND));
  Multiplexer #(.width(24), .enable("false")) multiplexer_4 (
    .in0(multiplexer_3_out), .in1({24{1'b0}}), .out(DIR_INPUT), .sel(LNa));
  Multiplexer #(.width(7), .enable("false")) multiplexer_5 (
    .in0(7'b0001010), .in1(print_udec_1_ascii), .out(ASCII), .sel(WAIT_q));
  D_Flip_Flop WAIT (.clk(CLK), .D(Write), .Q(WAIT_q), .en(or_8_out), .reset(CLR));  // open: Qn, preset
  or or_8 (or_8_out, Write, WriteEND);
  or or_9 (WASCII, print_udec_1_write_ascii, NEWLINE);
endmodule

module CONTROL_UNIT (
  input  CLK,
  input  C____Na,
  input  W___N,
  input  CLR,
  input  WriteEnd,
  input  Start,
  output LNa,
  output LN,
  output LC1,
  output LC2,
  output LW1,
  output LW2,
  output C__1,
  output C__2,
  output Write1,
  output END,
  output Write2,
  output NEWLINE1,
  output NEWLINE2,
  output NEWLINE3
);

  wire and_1_out, and_2_out, demultiplexer_1_out0, demultiplexer_1_out1, demultiplexer_4_out1,
       demultiplexer_5_out0, END_t, IDLE_q, or_1_out, or_2_out, or_4_out, or_6_out, WAIT_2_q, WAIT_5_q,
       WAIT_6_q, WAIT_7_q, WAIT_8_q, WAIT_9_q, WAIT_10_q, WAIT_12_q;

  D_Flip_Flop IDLE (.clk(CLK), .D(demultiplexer_1_out0), .Q(IDLE_q), .preset(CLR));  // open: Qn, en, reset
  Demultiplexer #(.enable("false")) demultiplexer_1 (
    .out0(demultiplexer_1_out0), .out1(demultiplexer_1_out1), .in(IDLE_q), .sel(Start));
  D_Flip_Flop WAIT (.clk(CLK), .D(demultiplexer_1_out1), .Q(LNa), .reset(CLR));  // open: Qn, preset, en
  D_Flip_Flop WAIT_2 (.clk(CLK), .D(LC2), .Q(WAIT_2_q), .reset(CLR));  // open: Qn, preset, en
  D_Flip_Flop WAIT_3 (.clk(CLK), .D(LNa), .Q(LN), .reset(CLR));  // open: Qn, preset, en
  or or_1 (or_1_out, WAIT_2_q, WAIT_7_q);
  Demultiplexer #(.enable("false")) demultiplexer_2 (.out0(END_t), .out1(LW2), .in(or_1_out), .sel(C____Na));
  D_Flip_Flop WAIT_4 (.clk(CLK), .D(LN), .Q(LC1), .reset(CLR));  // open: Qn, preset, en
  D_Flip_Flop WAIT_5 (.clk(CLK), .D(LW2), .Q(WAIT_5_q), .reset(CLR));  // open: Qn, preset, en
  or or_2 (or_2_out, WAIT_6_q, WAIT_10_q);
  D_Flip_Flop WAIT_6 (.clk(CLK), .D(LC1), .Q(WAIT_6_q), .reset(CLR));  // open: Qn, preset, en
  Demultiplexer #(.enable("false")) demultiplexer_3 (.out0(LC2), .out1(LW1), .in(or_2_out), .sel(C____Na));
  Demultiplexer #(.enable("false")) demultiplexer_4 (
    .out0(Write2), .out1(demultiplexer_4_out1), .in(WAIT_5_q), .sel(W___N));
  or or_3 (C__2, demultiplexer_4_out1, NEWLINE3);
  D_Flip_Flop WAIT_7 (.clk(CLK), .D(C__2), .Q(WAIT_7_q), .reset(CLR));  // open: Qn, preset, en
  D_Flip_Flop WAIT_8 (.clk(CLK), .D(LW1), .Q(WAIT_8_q), .reset(CLR));  // open: Qn, preset, en
  D_Flip_Flop WAIT_9 (.clk(CLK), .D(Write2), .Q(WAIT_9_q), .en(or_4_out), .reset(CLR));  // open: Qn, preset
  or or_4 (or_4_out, Write2, and_1_out);
  Demultiplexer #(.enable("false")) demultiplexer_5 (
    .out0(demultiplexer_5_out0), .out1(Write1), .in(WAIT_8_q), .sel(W___N));
  or or_5 (C__1, demultiplexer_5_out0, NEWLINE1);
  D_Flip_Flop WAIT_10 (.clk(CLK), .D(C__1), .Q(WAIT_10_q), .reset(CLR));  // open: Qn, preset, en
  and and_1 (and_1_out, WAIT_9_q, WriteEnd);
  D_Flip_Flop WAIT_11 (.clk(CLK), .D(and_1_out), .Q(NEWLINE3), .reset(CLR));  // open: Qn, preset, en
  D_Flip_Flop WAIT_12 (.clk(CLK), .D(Write1), .Q(WAIT_12_q), .en(or_6_out), .reset(CLR));  // open: Qn, preset
  or or_6 (or_6_out, Write1, and_2_out);
  and and_2 (and_2_out, WAIT_12_q, WriteEnd);
  D_Flip_Flop WAIT_13 (.clk(CLK), .D(and_2_out), .Q(NEWLINE1), .reset(CLR));  // open: Qn, preset, en
  D_Flip_Flop WAIT_14 (.clk(END_t), .D(END_t), .Q(END), .reset(CLR));  // open: Qn, preset, en

  assign NEWLINE2 = LC2;
endmodule
