// Logisim project Producto vectorial.circ as structural Verilog
module BOARD_BIG_ASM (
  output out_1
);

  wire button_1_out, CLK, CLR, d_ff_1_q, not_1_out, Write, Write_ASCII;
  wire [6:0] ASCII;
  wire [7:0] counter_1_q;
  wire [23:0] Dir_INPUT, Dir_MEMORY;
  wire [31:0] INPUT, MEMORY_IN, MEMORY_OUT;

  Button button_1 (.out(button_1_out));
  Clock clock_1 (.out(CLK));
  D_Flip_Flop d_ff_1 (.clk(CLK), .D(1'b1), .Q(d_ff_1_q), .reset(button_1_out));  // open: Qn, preset, en
  D_Flip_Flop d_ff_2 (.clk(CLK), .D(d_ff_1_q), .Qn(CLR), .reset(button_1_out));  // open: Q, preset, en
  BIG_ASM big_asm_1 (
    .DATA_INPUT(INPUT), .MEMORY_IN(MEMORY_OUT), .CLK(CLK), .CLR(CLR), .DIR_INPUT(Dir_INPUT),
    .MEMORY_OUT(MEMORY_IN), .DIR_MEMORY(Dir_MEMORY), .Write_OUTPUT(Write), .ASCII(ASCII),
    .Write_ASCII(Write_ASCII), .END(out_1));
  MEMORY memory_1 (.DIR(Dir_MEMORY), .DATA_IN(MEMORY_IN), .WRITE(Write), .CLK(CLK), .CLR(CLR), .DATA_OUT(MEMORY_OUT));
  INPUT input_1 (.DIR(Dir_INPUT), .CLK(CLK), .DATA_OUT(INPUT));
  Counter counter_1 (.load(1'b0), .count(not_1_out), .Q(counter_1_q), .clk(CLK), .clr(CLR));  // open: D, carry
  not not_1 (not_1_out, out_1);
  // Probe on counter_1_q
  TTY #(.rows(32), .cols(60)) tty_1 (.data(ASCII), .clk(CLK), .we(Write_ASCII), .clr(CLR));

  // Other names for the same wires on the sheet: END = out_1

  // Notes on the sheet:
  //   COUNTER
  //   BOARD
endmodule

module INPUT (
  input  [23:0] DIR,
  input  CLK,
  output [31:0] DATA_OUT
);

  RAM #(.addrWidth(24), .dataWidth(32)) ram_1 (.addr(DIR), .data(DATA_OUT), .clk(CLK), .ld(1'b1));  // open: sel, clr
endmodule

module MEMORY (
  input  [23:0] DIR,
  input  [31:0] DATA_IN,
  input  WRITE,
  input  CLK,
  input  CLR,
  output [31:0] DATA_OUT
);

  RAM #(.addrWidth(24), .dataWidth(32), .bus("separate")) ram_1 (
    .addr(DIR), .din(DATA_IN), .data(DATA_OUT), .str(WRITE), .clk(CLK), .clr(CLR));  // open: sel, ld
endmodule

module BIG_ASM (
  input  [31:0] DATA_INPUT,
  input  [31:0] MEMORY_IN,
  input  CLK,
  input  CLR,
  output [23:0] DIR_INPUT,
  output [31:0] MEMORY_OUT,
  output [23:0] DIR_MEMORY,
  output Write_OUTPUT,
  output [6:0] ASCII,
  output Write_ASCII,
  output END
);

  wire d_ff_3_q, d_ff_4_q, d_ff_7_q, END_t, FLAG, print_dec_1_end, print_dec_2_end, Start, W1, W2, W3, W4, W5;
  wire [6:0] multiplexer_1_out, multiplexer_2_out, P1, P2, P3;
  wire [31:0] N1, N2, N3;

  D_Flip_Flop d_ff_1 (.clk(CLK), .D(END_t), .Q(FLAG), .reset(CLR));  // open: Qn, preset, en
  PRINT_DEC print_dec_1 (
    .num(N1), .start(FLAG), .CLK(CLK), .RST(CLR), .ASCII(P1), .Write_ASCII(W1), .END(print_dec_1_end));
  D_Flip_Flop d_ff_2 (.clk(CLK), .D(print_dec_1_end), .Q(W2), .reset(CLR));  // open: Qn, preset, en
  D_Flip_Flop d_ff_3 (.clk(CLK), .D(1'b0), .Q(d_ff_3_q), .preset(CLR));  // open: Qn, en, reset
  D_Flip_Flop d_ff_4 (.clk(CLK), .D(W2), .Q(d_ff_4_q), .reset(CLR));  // open: Qn, preset, en
  D_Flip_Flop d_ff_5 (.clk(CLK), .D(d_ff_3_q), .Q(Start), .reset(CLR));  // open: Qn, preset, en
  CIRCUIT circuit_1 (
    .RESET(CLR), .START(Start), .out_9(END_t), .in_2(CLK), .Wx(N1), .Wy(N2), .Wz(N3), .Ux(DATA_INPUT),
    .out_5(DIR_INPUT));
  PRINT_DEC print_dec_2 (
    .num(N2), .start(d_ff_4_q), .CLK(CLK), .RST(CLR), .ASCII(P2), .Write_ASCII(W3), .END(print_dec_2_end));
  D_Flip_Flop d_ff_6 (.clk(CLK), .D(print_dec_2_end), .Q(W4), .reset(CLR));  // open: Qn, preset, en
  Multiplexer #(.width(7), .enable("false")) multiplexer_1 (
    .in0(7'b0101100), .in1(P3), .out(multiplexer_1_out), .sel(W5));
  D_Flip_Flop d_ff_7 (.clk(CLK), .D(W4), .Q(d_ff_7_q), .reset(CLR));  // open: Qn, preset, en
  Multiplexer #(.width(7), .enable("false")) multiplexer_2 (
    .in0(multiplexer_1_out), .in1(P2), .out(multiplexer_2_out), .sel(W3));
  Multiplexer #(.width(7), .enable("false")) multiplexer_3 (.in0(multiplexer_2_out), .in1(P1), .out(ASCII), .sel(W1));
  or or_1 (Write_ASCII, W1, W2, W3, W4, W5);
  PRINT_DEC print_dec_3 (.num(N3), .start(d_ff_7_q), .CLK(CLK), .RST(CLR), .ASCII(P3), .Write_ASCII(W5), .END(END));

  assign DIR_MEMORY = {24{1'b0}};
  assign MEMORY_OUT = {32{1'b0}};
  assign Write_OUTPUT = 1'b0;

  // Other names for the same wires on the sheet: Dir[23:0] = DIR_INPUT; N[31:0] = DATA_INPUT
endmodule

module PRINT_UDEC (
  input  [31:0] num,
  input  start,
  input  CLK,
  input  RST,
  output [6:0] ASCII,
  output Write_ASCII,
  output \end 
);

  wire _0_c, _0_n, demultiplexer_1_out0, demultiplexer_2_out0, demultiplexer_2_out1, demultiplexer_3_out0,
       demultiplexer_3_out1, IDLE_2_q, IDLE_3_q, IDLE_4_q, IDLE_q, Lc, Lc_0, Ln, Ln_0, or_1_out;
  wire [23:0] bit_extender_1_out;
  wire [31:0] c, c___1, c___1_t, divider_1_rem, memory_1_data_out, multiplexer_1_out, multiplexer_2_out,
       multiplexer_3_out, n, n___10, n___10___48;

  Multiplexer #(.width(32), .enable("false")) multiplexer_1 (
    .in0(num), .in1(n___10), .out(multiplexer_1_out), .sel(Lc_0));
  Divider #(.width(32)) divider_1 (.a(n), .b(32'ha), .out(n___10), .rem(divider_1_rem));  // open: upper
  Adder #(.width(32)) adder_1 (.a(divider_1_rem), .b(32'h30), .out(n___10___48));  // open: cin, cout
  or or_1 (or_1_out, demultiplexer_1_out0, \end );
  Register #(.width(32)) u_n (.D(multiplexer_1_out), .en(Ln), .Q(n), .clk(CLK), .clr(RST));
  D_Flip_Flop IDLE (.clk(CLK), .D(or_1_out), .Q(IDLE_q), .preset(RST));  // open: Qn, en, reset
  Demultiplexer #(.enable("false")) demultiplexer_1 (
    .out0(demultiplexer_1_out0), .out1(Ln_0), .in(IDLE_q), .sel(start));
  or or_2 (Write_ASCII, demultiplexer_3_out0, demultiplexer_2_out1);
  Multiplexer #(.width(32), .enable("false")) multiplexer_2 (
    .in0(c___1), .in1(c___1_t), .out(multiplexer_2_out), .sel(Write_ASCII));
  Adder #(.width(32)) adder_2 (.a(c), .b(32'h1), .out(c___1));  // open: cin, cout
  Subtractor #(.width(32)) subtractor_1 (.a(c), .b(32'h1), .out(c___1_t));  // open: bin, bout
  D_Flip_Flop IDLE_2 (.clk(CLK), .D(Ln_0), .Q(IDLE_2_q), .reset(RST));  // open: Qn, preset, en
  Register #(.width(32)) u_c (.D(multiplexer_2_out), .en(Lc), .Q(c), .clk(CLK), .clr(RST));
  or or_3 (Lc_0, IDLE_2_q, demultiplexer_3_out1);
  Multiplexer #(.width(32), .enable("false")) multiplexer_3 (
    .in0(c), .in1(c___1_t), .out(multiplexer_3_out), .sel(Write_ASCII));
  Comparator #(.width(32), .mode("unsigned")) comparator_1 (.a({32{1'b0}}), .b(n), .lt(_0_n));  // open: gt, eq
  Comparator #(.width(32), .mode("unsigned")) comparator_2 (.a({32{1'b0}}), .b(c), .lt(_0_c));  // open: gt, eq
  D_Flip_Flop IDLE_3 (.clk(CLK), .D(Write_ASCII), .Q(IDLE_3_q), .reset(RST));  // open: Qn, preset, en
  Demultiplexer #(.enable("false")) demultiplexer_2 (
    .out0(demultiplexer_2_out0), .out1(demultiplexer_2_out1), .in(IDLE_3_q), .sel(_0_c));
  Bit_Extender #(.in_width(32), .out_width(24)) bit_extender_1 (.in(multiplexer_3_out), .out(bit_extender_1_out));
  D_Flip_Flop IDLE_4 (.clk(CLK), .D(Lc_0), .Q(IDLE_4_q), .reset(RST));  // open: Qn, preset, en
  or or_4 (Lc, Lc_0, Write_ASCII);
  or or_5 (Ln, Ln_0, Lc_0);
  Demultiplexer #(.enable("false")) demultiplexer_3 (
    .out0(demultiplexer_3_out0), .out1(demultiplexer_3_out1), .in(IDLE_4_q), .sel(_0_n));
  D_Flip_Flop IDLE_5 (.clk(CLK), .D(demultiplexer_2_out0), .Q(\end ), .reset(RST));  // open: Qn, preset, en
  MEMORY memory_1 (
    .DIR(bit_extender_1_out), .DATA_IN(n___10___48), .WRITE(Lc_0), .CLK(CLK), .CLR(RST),
    .DATA_OUT(memory_1_data_out));
  Bit_Extender #(.in_width(32), .out_width(7)) bit_extender_2 (.in(memory_1_data_out), .out(ASCII));

  // Other names for the same wires on the sheet: Lc_1 = Write_ASCII; Sc = Write_ASCII; Ln_1 = Lc_0; Sn = Lc_0;
  //   Write = Lc_0
endmodule

module PRINT_DEC (
  input  [31:0] num,
  input  start,
  input  CLK,
  input  RST,
  output [6:0] ASCII,
  output Write_ASCII,
  output END
);

  wire demultiplexer_1_out0, demultiplexer_1_out1, demultiplexer_2_out0, demultiplexer_3_out0, end_t,
       IDLE_3_q, IDLE_q, or_1_out, or_2_out, or_3_out, S_ASCII, startUDEC, Write_ASCII_1;
  wire [6:0] ASCII_t;
  wire [31:0] multiplexer_1_out, negator_1_out;

  or or_1 (or_1_out, demultiplexer_1_out0, END);
  Negator #(.width(32)) negator_1 (.in(num), .out(negator_1_out));
  D_Flip_Flop IDLE (.clk(CLK), .D(or_1_out), .Q(IDLE_q), .preset(RST));  // open: Qn, en, reset
  Demultiplexer #(.enable("false")) demultiplexer_1 (
    .out0(demultiplexer_1_out0), .out1(demultiplexer_1_out1), .in(IDLE_q), .sel(start));
  Multiplexer #(.width(32), .enable("false")) multiplexer_1 (
    .in0(num), .in1(negator_1_out), .out(multiplexer_1_out), .sel(num[31]));
  Demultiplexer #(.enable("false")) demultiplexer_2 (
    .out0(demultiplexer_2_out0), .out1(S_ASCII), .in(demultiplexer_1_out1), .sel(num[31]));
  or or_2 (or_2_out, demultiplexer_2_out0, S_ASCII);
  D_Flip_Flop IDLE_2 (.clk(CLK), .D(or_2_out), .Q(startUDEC), .reset(RST));  // open: Qn, preset, en
  PRINT_UDEC print_udec_1 (
    .num(multiplexer_1_out), .start(startUDEC), .CLK(CLK), .RST(RST), .ASCII(ASCII_t),
    .Write_ASCII(Write_ASCII_1), .\end (end_t));
  D_Flip_Flop IDLE_3 (.clk(CLK), .D(or_3_out), .Q(IDLE_3_q), .reset(RST));  // open: Qn, preset, en
  or or_3 (or_3_out, startUDEC, demultiplexer_3_out0);
  Demultiplexer #(.enable("false")) demultiplexer_3 (
    .out0(demultiplexer_3_out0), .out1(END), .in(IDLE_3_q), .sel(end_t));
  Multiplexer #(.width(7), .enable("false")) multiplexer_2 (
    .in0(ASCII_t), .in1(7'b0101101), .out(ASCII), .sel(S_ASCII));
  or or_4 (Write_ASCII, S_ASCII, Write_ASCII_1);

  // Other names for the same wires on the sheet: sign = num[31]; Write_ASCII_0 = S_ASCII
endmodule

module TEST_PRINT (
  input  [31:0] in_1,
  output out_2
);

  wire button_1_out, button_2_out, CLK, CLR, d_ff_1_q, Write_ASCII;
  wire [6:0] ASCII;

  Button button_1 (.out(button_1_out));
  Clock clock_1 (.out(CLK));
  D_Flip_Flop d_ff_1 (.clk(CLK), .D(1'b1), .Q(d_ff_1_q), .reset(button_1_out));  // open: Qn, preset, en
  D_Flip_Flop d_ff_2 (.clk(CLK), .D(d_ff_1_q), .Qn(CLR), .reset(button_1_out));  // open: Q, preset, en
  Button button_2 (.out(button_2_out));
  PRINT_UDEC print_udec_1 ();  // open: num, start, CLK, RST, ASCII, Write_ASCII, end
  PRINT_DEC print_dec_1 (
    .num(in_1), .start(button_2_out), .CLK(CLK), .RST(CLR), .ASCII(ASCII), .Write_ASCII(Write_ASCII),
    .END(out_2));
  TTY #(.rows(32), .cols(60)) tty_1 (.data(ASCII), .clk(CLK), .we(Write_ASCII), .clr(CLR));
endmodule

module DATA_PATH (
  input  [31:0] Ux,
  input  in_2,
  input  in_3,
  input  in_4,
  input  in_5,
  input  in_6,
  input  in_7,
  input  in_8,
  input  CLOCK,
  input  in_10,
  output [31:0] Wx,
  output [31:0] Wy,
  output [31:0] Wz,
  output [23:0] Dir
);

  wire [23:0] multiplexer_1_out, multiplexer_2_out, multiplexer_3_out, multiplexer_4_out;
  wire [31:0] Ux_t, UxVy, UxVy___UyVx, UxVz, Uy, UyVx, UyVz, UyVz___UzVy, Uz, UzVx, UzVx___UxVz, UzVy, Vx,
       Vy, Vz;

  Multiplier #(.width(32)) multiplier_1 (.a(Uy), .b(Vz), .out(UyVz));  // open: cin, cout
  Multiplier #(.width(32)) multiplier_2 (.a(Uz), .b(Vy), .out(UzVy));  // open: cin, cout
  Multiplier #(.width(32)) multiplier_3 (.a(Uz), .b(Vx), .out(UzVx));  // open: cin, cout
  Multiplier #(.width(32)) multiplier_4 (.a(Ux_t), .b(Vz), .out(UxVz));  // open: cin, cout
  Multiplier #(.width(32)) multiplier_5 (.a(Ux_t), .b(Vy), .out(UxVy));  // open: cin, cout
  Multiplier #(.width(32)) multiplier_6 (.a(Uy), .b(Vx), .out(UyVx));  // open: cin, cout
  Register #(.width(32)) R (.D(Ux), .en(in_2), .Q(Ux_t), .clk(CLOCK), .clr(in_10));
  Register #(.width(32)) R_2 (.D(Ux), .en(in_3), .Q(Uy), .clk(CLOCK), .clr(in_10));
  Subtractor #(.width(32)) subtractor_1 (.a(UyVz), .b(UzVy), .out(UyVz___UzVy));  // open: bin, bout
  Register #(.width(32)) R_3 (.D(Ux), .en(in_4), .Q(Uz), .clk(CLOCK), .clr(in_10));
  Register #(.width(32)) R_4 (.D(UyVz___UzVy), .en(in_8), .Q(Wx), .clk(CLOCK), .clr(in_10));
  Register #(.width(32)) R_5 (.D(Ux), .en(in_5), .Q(Vx), .clk(CLOCK), .clr(in_10));
  Subtractor #(.width(32)) subtractor_2 (.a(UzVx), .b(UxVz), .out(UzVx___UxVz));  // open: bin, bout
  Register #(.width(32)) R_6 (.D(UxVy___UyVx), .en(in_8), .Q(Wz), .clk(CLOCK), .clr(in_10));
  Register #(.width(32)) R_7 (.D(Ux), .en(in_6), .Q(Vy), .clk(CLOCK), .clr(in_10));
  Register #(.width(32)) R_8 (.D(UzVx___UxVz), .en(in_8), .Q(Wy), .clk(CLOCK), .clr(in_10));
  Register #(.width(32)) R_9 (.D(Ux), .en(in_7), .Q(Vz), .clk(CLOCK), .clr(in_10));
  Multiplexer #(.width(24), .enable("false")) multiplexer_1 (
    .in0(24'h5), .in1(24'h4), .out(multiplexer_1_out), .sel(in_6));
  Subtractor #(.width(32)) subtractor_3 (.a(UxVy), .b(UyVx), .out(UxVy___UyVx));  // open: bin, bout
  Multiplexer #(.width(24), .enable("false")) multiplexer_2 (
    .in0(multiplexer_1_out), .in1(24'h3), .out(multiplexer_2_out), .sel(in_5));
  Multiplexer #(.width(24), .enable("false")) multiplexer_3 (
    .in0(multiplexer_2_out), .in1(24'h2), .out(multiplexer_3_out), .sel(in_4));
  Multiplexer #(.width(24), .enable("false")) multiplexer_4 (
    .in0(multiplexer_3_out), .in1(24'h1), .out(multiplexer_4_out), .sel(in_3));
  Multiplexer #(.width(24), .enable("false")) multiplexer_5 (
    .in0(multiplexer_4_out), .in1({24{1'b0}}), .out(Dir), .sel(in_2));

  // Other names for the same wires on the sheet: CLR = in_10; L0 = in_2; L1 = in_3; L2 = in_4; L3 = in_5; L4 = in_6;
  //   L5 = in_7; N[31:0] = Ux; Start = in_8
endmodule

module CONTROL_UNIT (
  input  START,
  input  RESET,
  input  CLOCK,
  output out_4,
  output out_5,
  output out_6,
  output out_7,
  output out_8,
  output out_9,
  output END
);

  wire demultiplexer_1_out0, IDLE_q;

  Demultiplexer #(.enable("false")) demultiplexer_1 (
    .out0(demultiplexer_1_out0), .out1(out_4), .in(IDLE_q), .sel(START));
  D_Flip_Flop IDLE (.clk(CLOCK), .D(demultiplexer_1_out0), .Q(IDLE_q), .preset(RESET));  // open: Qn, en, reset
  D_Flip_Flop WAIT (.clk(CLOCK), .D(out_4), .Q(out_5), .reset(RESET));  // open: Qn, preset, en
  D_Flip_Flop WAIT_2 (.clk(CLOCK), .D(out_5), .Q(out_6), .reset(RESET));  // open: Qn, preset, en
  D_Flip_Flop WAIT_3 (.clk(CLOCK), .D(out_6), .Q(out_7), .reset(RESET));  // open: Qn, preset, en
  D_Flip_Flop WAIT_4 (.clk(CLOCK), .D(out_7), .Q(out_8), .reset(RESET));  // open: Qn, preset, en
  D_Flip_Flop WAIT_5 (.clk(CLOCK), .D(out_8), .Q(out_9), .reset(RESET));  // open: Qn, preset, en
  D_Flip_Flop u_END (.clk(CLOCK), .D(out_9), .Q(END), .reset(RESET));  // open: Qn, preset, en

  // Other names for the same wires on the sheet: L0 = out_4; L1 = out_5; L2 = out_6; L3 = out_7; L4 = out_8;
  //   L5 = out_9
endmodule

module CIRCUIT (
  input  [31:0] Ux,
  input  in_2,
  input  RESET,
  input  START,
  output [23:0] out_5,
  output [31:0] Wx,
  output [31:0] Wy,
  output [31:0] Wz,
  output out_9
);

  wire control_unit_1_out_4, control_unit_1_out_5, control_unit_1_out_6, control_unit_1_out_7,
       control_unit_1_out_8, control_unit_1_out_9;

  CONTROL_UNIT control_unit_1 (
    .START(START), .RESET(RESET), .END(out_9), .CLOCK(in_2), .out_5(control_unit_1_out_5),
    .out_6(control_unit_1_out_6), .out_7(control_unit_1_out_7), .out_8(control_unit_1_out_8),
    .out_9(control_unit_1_out_9), .out_4(control_unit_1_out_4));
  DATA_PATH data_path_1 (
    .CLOCK(in_2), .Ux(Ux), .Wx(Wx), .Wy(Wy), .Wz(Wz), .in_2(control_unit_1_out_4),
    .in_3(control_unit_1_out_5), .in_4(control_unit_1_out_6), .in_5(control_unit_1_out_7),
    .in_6(control_unit_1_out_8), .in_7(control_unit_1_out_9), .in_10(RESET), .in_8(out_9), .Dir(out_5));

  // Other names for the same wires on the sheet: CLOCK = in_2; END = out_9; N[31:0] = Ux
endmodule

module TEST_CIRCUIT (
  output out_1,
  output [31:0] Wx,
  output [31:0] Wy,
  output [31:0] Wz
);

  wire CLOCK, R_out, S_out;
  wire [31:0] Ux, Uy, Uz, Vx, Vy, Vz;

  Clock clock_1 (.out(CLOCK));
  // Probe on Uy
  // Probe on Uz
  // Probe on Vx
  // Probe on Vy
  // Probe on Vz
  Button S (.out(S_out));
  // Probe on Ux
  Button R (.out(R_out));
  // CIRCUIT circuit_1: pin names not known; wires that end beside it: S_out, Ux, Uy, Uz, Vx, Vy, Vz, CLOCK, R_out, out_1, Wx, Wy, Wz
  // Probe on Wx
  // Probe on Wy
  // Probe on Wz
endmodule
