// Logisim project Problema83.circ as structural Verilog
module BOARD_BIG_ASM (
  output out_1
);

  wire button_1_out, CLK, CLR, d_ff_1_q, not_1_out, Write, Write_ASCII;
  wire [6:0] ASCII;
  wire [7:0] counter_1_q;
  wire [23:0] Dir_INPUT, Dir_MEMORY;
  wire [31:0] INPUT, MEMORY_IN, MEMORY_OUT;

  Button button_1 (.out(button_1_out));
  Clock clock_1 (.out(CLK));
  D_Flip_Flop d_ff_1 (.clk(CLK), .D(1'b1), .Q(d_ff_1_q), .reset(button_1_out));  // open: Qn, preset, en
  D_Flip_Flop d_ff_2 (.clk(CLK), .D(d_ff_1_q), .Qn(CLR), .reset(button_1_out));  // open: Q, preset, en
  BIG_ASM big_asm_1 (
    .DATA_INPUT(INPUT), .MEMORY_IN(MEMORY_OUT), .CLK(CLK), .CLR(CLR), .DIR_INPUT(Dir_INPUT),
    .MEMORY_OUT(MEMORY_IN), .DIR_MEMORY(Dir_MEMORY), .Write_OUTPUT(Write), .ASCII(ASCII),
    .Write_ASCII(Write_ASCII), .END(out_1));
  MEMORY memory_1 (.DIR(Dir_MEMORY), .DATA_IN(MEMORY_IN), .WRITE(Write), .CLK(CLK), .CLR(CLR), .DATA_OUT(MEMORY_OUT));
  INPUT input_1 (.DIR(Dir_INPUT), .CLK(CLK), .DATA_OUT(INPUT));
  Counter counter_1 (.load(1'b0), .count(not_1_out), .Q(counter_1_q), .clk(CLK), .clr(CLR));  // open: D, carry
  not not_1 (not_1_out, out_1);
  // Probe on counter_1_q
  TTY #(.rows(32), .cols(60)) tty_1 (.data(ASCII), .clk(CLK), .we(Write_ASCII), .clr(CLR));

  // Other names for the same wires on the sheet: END = out_1

  // Notes on the sheet:
  //   COUNTER
  //   BOARD
endmodule

module INPUT (
  input  [23:0] DIR,
  input  CLK,
  output [31:0] DATA_OUT
);

  RAM #(.addrWidth(24), .dataWidth(32)) ram_1 (.addr(DIR), .data(DATA_OUT), .clk(CLK), .ld(1'b1));  // open: sel, clr
endmodule

module MEMORY (
  input  [23:0] DIR,
  input  [31:0] DATA_IN,
  input  WRITE,
  input  CLK,
  input  CLR,
  output [31:0] DATA_OUT
);

  RAM #(.addrWidth(24), .dataWidth(32), .bus("separate")) ram_1 (
    .addr(DIR), .din(DATA_IN), .data(DATA_OUT), .str(WRITE), .clk(CLK), .clr(CLR));  // open: sel, ld
endmodule

module BIG_ASM (
  input  [31:0] DATA_INPUT,
  input  [31:0] MEMORY_IN,
  input  CLK,
  input  CLR,
  output [23:0] DIR_INPUT,
  output [31:0] MEMORY_OUT,
  output [23:0] DIR_MEMORY,
  output Write_OUTPUT,
  output [6:0] ASCII,
  output Write_ASCII,
  output END
);

  wire A_____1, CALL1, CALL2, CALL3, IDLE_q, LA, LCTR, LF, LN, LP1, LP2, P_2___1___N, P_2___2___N, PUSH01,
       PUSH1, PUSH02, PUSH2, PUSHP1, PUSHP2, RET, Start, Write;
  wire [31:0] data_path_1_out_30, data_path_1_out_31, data_path_1_out_32, F;

  D_Flip_Flop IDLE (.clk(CLK), .D(1'b0), .Q(IDLE_q), .preset(CLR));  // open: Qn, en, reset
  D_Flip_Flop IDLE_2 (.clk(CLK), .D(IDLE_q), .Q(Start), .reset(CLR));  // open: Qn, preset, en
  // Probe on data_path_1_out_31
  // Probe on data_path_1_out_32
  // Probe on data_path_1_out_30
  DATA_PATH data_path_1 (
    .CLK(CLK), .DATA_INPUT(DATA_INPUT), .CLR(CLR), .LCTR(LCTR), .LN(LN), .LP1(LP1), .LP2(LP2), .LA(LA),
    .LF(LF), .Write(Write), .CALL1(CALL1), .CALL2(CALL2), .CALL3(CALL3), .RET(RET), .PUSH01(PUSH01),
    .PUSH02(PUSH02), .PUSH1(PUSH1), .PUSH2(PUSH2), .PUSHP1(PUSHP1), .MEMORY_IN(MEMORY_IN), .PUSHP2(PUSHP2),
    .DIR_INPUT(DIR_INPUT), .MEMORY_OUT(MEMORY_OUT), .DIR_MEMORY(DIR_MEMORY), .Write_OUTPUT(Write_OUTPUT),
    .F(F), .A_____1(A_____1), .P_2_1___N(P_2___1___N), .P_2_2___N(P_2___2___N), .ASCII(ASCII),
    .WASCII(Write_ASCII), .out_30(data_path_1_out_30), .out_32(data_path_1_out_32),
    .out_31(data_path_1_out_31));
  CONTROL_UNIT control_unit_1 (
    .CLK(CLK), .CLR(CLR), .Start(Start), .A_____1(A_____1), .F(F), .P_2_1___N(P_2___1___N),
    .P_2_2___N(P_2___2___N), .LN(LN), .LP1(LP1), .LP2(LP2), .LA(LA), .LCTR(LCTR), .LF(LF), .RET(RET),
    .CALL1(CALL1), .CALL2(CALL2), .CALL3(CALL3), .PUSH01(PUSH01), .PUSH02(PUSH02), .PUSH1(PUSH1),
    .PUSH2(PUSH2), .PUSHP1(PUSHP1), .Write(Write), .PUSHP2(PUSHP2), .END(END));  // open: INVALID

  // Other names for the same wires on the sheet: DI[31:0] = DATA_INPUT; DIRI[23:0] = DIR_INPUT;
  //   DIRM[23:0] = DIR_MEMORY; MI[31:0] = MEMORY_IN; MO[31:0] = MEMORY_OUT; WASCII = Write_ASCII
endmodule

module PRINT_UDEC (
  input  [31:0] num,
  input  start,
  input  CLK,
  input  RST,
  output [6:0] ASCII,
  output Write_ASCII,
  output \end 
);

  wire _0_c, _0_n, demultiplexer_1_out0, demultiplexer_2_out0, demultiplexer_2_out1, demultiplexer_3_out0,
       demultiplexer_3_out1, IDLE_2_q, IDLE_3_q, IDLE_4_q, IDLE_q, Lc, Lc_0, Ln, Ln_0, or_1_out;
  wire [23:0] bit_extender_1_out;
  wire [31:0] c, c___1, c___1_t, divider_1_rem, memory_1_data_out, multiplexer_1_out, multiplexer_2_out,
       multiplexer_3_out, n, n___10, n___10___48;

  Multiplexer #(.width(32), .enable("false")) multiplexer_1 (
    .in0(num), .in1(n___10), .out(multiplexer_1_out), .sel(Lc_0));
  Divider #(.width(32)) divider_1 (.a(n), .b(32'ha), .out(n___10), .rem(divider_1_rem));  // open: upper
  Adder #(.width(32)) adder_1 (.a(divider_1_rem), .b(32'h30), .out(n___10___48));  // open: cin, cout
  or or_1 (or_1_out, demultiplexer_1_out0, \end );
  Register #(.width(32)) u_n (.D(multiplexer_1_out), .en(Ln), .Q(n), .clk(CLK), .clr(RST));
  D_Flip_Flop IDLE (.clk(CLK), .D(or_1_out), .Q(IDLE_q), .preset(RST));  // open: Qn, en, reset
  Demultiplexer #(.enable("false")) demultiplexer_1 (
    .out0(demultiplexer_1_out0), .out1(Ln_0), .in(IDLE_q), .sel(start));
  or or_2 (Write_ASCII, demultiplexer_3_out0, demultiplexer_2_out1);
  Multiplexer #(.width(32), .enable("false")) multiplexer_2 (
    .in0(c___1), .in1(c___1_t), .out(multiplexer_2_out), .sel(Write_ASCII));
  Adder #(.width(32)) adder_2 (.a(c), .b(32'h1), .out(c___1));  // open: cin, cout
  Subtractor #(.width(32)) subtractor_1 (.a(c), .b(32'h1), .out(c___1_t));  // open: bin, bout
  D_Flip_Flop IDLE_2 (.clk(CLK), .D(Ln_0), .Q(IDLE_2_q), .reset(RST));  // open: Qn, preset, en
  Register #(.width(32)) u_c (.D(multiplexer_2_out), .en(Lc), .Q(c), .clk(CLK), .clr(RST));
  or or_3 (Lc_0, IDLE_2_q, demultiplexer_3_out1);
  Multiplexer #(.width(32), .enable("false")) multiplexer_3 (
    .in0(c), .in1(c___1_t), .out(multiplexer_3_out), .sel(Write_ASCII));
  Comparator #(.width(32), .mode("unsigned")) comparator_1 (.a({32{1'b0}}), .b(n), .lt(_0_n));  // open: gt, eq
  Comparator #(.width(32), .mode("unsigned")) comparator_2 (.a({32{1'b0}}), .b(c), .lt(_0_c));  // open: gt, eq
  D_Flip_Flop IDLE_3 (.clk(CLK), .D(Write_ASCII), .Q(IDLE_3_q), .reset(RST));  // open: Qn, preset, en
  Demultiplexer #(.enable("false")) demultiplexer_2 (
    .out0(demultiplexer_2_out0), .out1(demultiplexer_2_out1), .in(IDLE_3_q), .sel(_0_c));
  Bit_Extender #(.in_width(32), .out_width(24)) bit_extender_1 (.in(multiplexer_3_out), .out(bit_extender_1_out));
  D_Flip_Flop IDLE_4 (.clk(CLK), .D(Lc_0), .Q(IDLE_4_q), .reset(RST));  // open: Qn, preset, en
  or or_4 (Lc, Lc_0, Write_ASCII);
  or or_5 (Ln, Ln_0, Lc_0);
  Demultiplexer #(.enable("false")) demultiplexer_3 (
    .out0(demultiplexer_3_out0), .out1(demultiplexer_3_out1), .in(IDLE_4_q), .sel(_0_n));
  D_Flip_Flop IDLE_5 (.clk(CLK), .D(demultiplexer_2_out0), .Q(\end ), .reset(RST));  // open: Qn, preset, en
  MEMORY memory_1 (
    .DIR(bit_extender_1_out), .DATA_IN(n___10___48), .WRITE(Lc_0), .CLK(CLK), .CLR(RST),
    .DATA_OUT(memory_1_data_out));
  Bit_Extender #(.in_width(32), .out_width(7)) bit_extender_2 (.in(memory_1_data_out), .out(ASCII));

  // Other names for the same wires on the sheet: Lc_1 = Write_ASCII; Sc = Write_ASCII; Ln_1 = Lc_0; Sn = Lc_0;
  //   Write = Lc_0
endmodule

module PRINT_DEC (
  input  [31:0] num,
  input  start,
  input  CLK,
  input  RST,
  output [6:0] ASCII,
  output Write_ASCII,
  output END
);

  wire demultiplexer_1_out0, demultiplexer_1_out1, demultiplexer_2_out0, demultiplexer_3_out0, end_t,
       IDLE_3_q, IDLE_q, or_1_out, or_2_out, or_3_out, S_ASCII, startUDEC, Write_ASCII_1;
  wire [6:0] ASCII_t;
  wire [31:0] multiplexer_1_out, negator_1_out;

  or or_1 (or_1_out, demultiplexer_1_out0, END);
  Negator #(.width(32)) negator_1 (.in(num), .out(negator_1_out));
  D_Flip_Flop IDLE (.clk(CLK), .D(or_1_out), .Q(IDLE_q), .preset(RST));  // open: Qn, en, reset
  Demultiplexer #(.enable("false")) demultiplexer_1 (
    .out0(demultiplexer_1_out0), .out1(demultiplexer_1_out1), .in(IDLE_q), .sel(start));
  Multiplexer #(.width(32), .enable("false")) multiplexer_1 (
    .in0(num), .in1(negator_1_out), .out(multiplexer_1_out), .sel(num[31]));
  Demultiplexer #(.enable("false")) demultiplexer_2 (
    .out0(demultiplexer_2_out0), .out1(S_ASCII), .in(demultiplexer_1_out1), .sel(num[31]));
  or or_2 (or_2_out, demultiplexer_2_out0, S_ASCII);
  D_Flip_Flop IDLE_2 (.clk(CLK), .D(or_2_out), .Q(startUDEC), .reset(RST));  // open: Qn, preset, en
  PRINT_UDEC print_udec_1 (
    .num(multiplexer_1_out), .start(startUDEC), .CLK(CLK), .RST(RST), .ASCII(ASCII_t),
    .Write_ASCII(Write_ASCII_1), .\end (end_t));
  D_Flip_Flop IDLE_3 (.clk(CLK), .D(or_3_out), .Q(IDLE_3_q), .reset(RST));  // open: Qn, preset, en
  or or_3 (or_3_out, startUDEC, demultiplexer_3_out0);
  Demultiplexer #(.enable("false")) demultiplexer_3 (
    .out0(demultiplexer_3_out0), .out1(END), .in(IDLE_3_q), .sel(end_t));
  Multiplexer #(.width(7), .enable("false")) multiplexer_2 (
    .in0(ASCII_t), .in1(7'b0101101), .out(ASCII), .sel(S_ASCII));
  or or_4 (Write_ASCII, S_ASCII, Write_ASCII_1);

  // Other names for the same wires on the sheet: sign = num[31]; Write_ASCII_0 = S_ASCII
endmodule

module TEST_PRINT (
  input  [31:0] in_1,
  output out_2
);

  wire button_1_out, button_2_out, CLK, CLR, d_ff_1_q, Write_ASCII;
  wire [6:0] ASCII;

  Button button_1 (.out(button_1_out));
  Clock clock_1 (.out(CLK));
  D_Flip_Flop d_ff_1 (.clk(CLK), .D(1'b1), .Q(d_ff_1_q), .reset(button_1_out));  // open: Qn, preset, en
  D_Flip_Flop d_ff_2 (.clk(CLK), .D(d_ff_1_q), .Qn(CLR), .reset(button_1_out));  // open: Q, preset, en
  Button button_2 (.out(button_2_out));
  PRINT_UDEC print_udec_1 ();  // open: num, start, CLK, RST, ASCII, Write_ASCII, end
  PRINT_DEC print_dec_1 (
    .num(in_1), .start(button_2_out), .CLK(CLK), .RST(CLR), .ASCII(ASCII), .Write_ASCII(Write_ASCII),
    .END(out_2));
  TTY #(.rows(32), .cols(60)) tty_1 (.data(ASCII), .clk(CLK), .we(Write_ASCII), .clr(CLR));
endmodule

module DATA_PATH (
  input  CLK,
  input  [31:0] DATA_INPUT,
  input  CLR,
  input  LCTR,
  input  LN,
  input  LP1,
  input  LP2,
  input  LA,
  input  LF,
  input  Write,
  input  CALL1,
  input  CALL2,
  input  CALL3,
  input  RET,
  input  PUSH01,
  input  PUSH02,
  input  PUSH1,
  input  PUSH2,
  input  PUSHP1,
  input  [31:0] MEMORY_IN,
  input  PUSHP2,
  output [23:0] DIR_INPUT,
  output [31:0] MEMORY_OUT,
  output [23:0] DIR_MEMORY,
  output Write_OUTPUT,
  output [31:0] F,
  output A_____1,
  output P_2_1___N,
  output P_2_2___N,
  output [31:0] out_30,
  output [31:0] out_31,
  output [31:0] out_32,
  output [6:0] ASCII,
  output WASCII
);

  wire adder_4_cout, CALL, LP, or_1_out, or_3_out, or_4_out;
  wire [23:0] adder_2_out, adder_3_out, multiplexer_1_out, multiplexer_3_out, subtractor_2_out;
  wire [31:0] A, adder_1_out, CTR, multiplexer_2_out, multiplexer_6_out, multiplexer_7_out,
       multiplexer_8_out, N, negator_1_out, P_2_1, P_2_2, shifter_1_out, subtractor_1_out;

  Subtractor #(.width(32)) subtractor_1 (.a(out_32), .b(32'h2), .out(subtractor_1_out));  // open: bin, bout
  Subtractor #(.width(24)) subtractor_2 (.a(out_32[23:0]), .b(24'h1), .out(subtractor_2_out));  // open: bin, bout
  Multiplexer #(.width(24), .enable("false")) multiplexer_1 (
    .in0(subtractor_2_out), .in1(out_32[23:0]), .out(multiplexer_1_out), .sel(LF));
  Multiplexer #(.width(32), .enable("false")) multiplexer_2 (
    .in0(subtractor_1_out), .in1(adder_1_out), .out(multiplexer_2_out), .sel(CALL));
  or or_1 (or_1_out, CALL, RET);
  Adder #(.width(32)) adder_1 (.a(32'h2), .b(out_32), .out(adder_1_out));  // open: cin, cout
  or or_2 (CALL, CALL1, CALL2, CALL3);
  Register #(.width(32)) register_1 (.D(multiplexer_2_out), .en(or_1_out), .Q(out_32), .clk(CLK), .clr(CLR));
  Register #(.width(32)) register_2 (.D(MEMORY_IN), .en(LP), .Q(out_30), .clk(CLK), .clr(CLR));
  or or_3 (or_3_out, PUSH01, PUSH1, PUSH2);
  Multiplexer #(.width(24), .enable("false")) multiplexer_3 (
    .in0(multiplexer_1_out), .in1(out_32[23:0]), .out(multiplexer_3_out), .sel(or_3_out));
  Adder #(.width(24)) adder_2 (.a(out_32[23:0]), .b(24'h1), .out(adder_2_out));  // open: cin, cout
  or or_4 (or_4_out, PUSH02, PUSHP1, PUSHP2);
  Register #(.width(32)) register_3 (.D(MEMORY_IN), .en(LF), .Q(F), .clk(CLK), .clr(CLR));
  Multiplexer #(.width(24), .enable("false")) multiplexer_4 (
    .in0(multiplexer_3_out), .in1(adder_2_out), .out(DIR_MEMORY), .sel(or_4_out));
  or or_5 (LP, LP1, LP2);
  Register #(.width(32)) register_4 (.D(DATA_INPUT), .en(LN), .Q(N), .clk(CLK), .clr(CLR));
  Adder #(.width(24)) adder_3 (.a(out_30[23:0]), .b(24'h1), .out(adder_3_out));  // open: cin, cout
  Register #(.width(32)) register_5 (.D(DATA_INPUT), .en(LA), .Q(A), .clk(CLK), .clr(CLR));
  Multiplexer #(.width(24), .enable("false")) multiplexer_5 (
    .in0({24{1'b0}}), .in1(adder_3_out), .out(DIR_INPUT), .sel(LA));
  Multiplexer #(.width(32), .enable("false")) multiplexer_6 (
    .in0({32{1'b0}}), .in1(P_2_2), .out(multiplexer_6_out), .sel(PUSHP2));
  Multiplexer #(.width(32), .enable("false")) multiplexer_7 (
    .in0(multiplexer_6_out), .in1(P_2_1), .out(multiplexer_7_out), .sel(PUSHP1));
  or or_6 (Write_OUTPUT, PUSH01, PUSH02, PUSH1, PUSH2, PUSHP1, PUSHP2);
  Multiplexer #(.width(32), .enable("false")) multiplexer_8 (
    .in0(multiplexer_7_out), .in1(32'h2), .out(multiplexer_8_out), .sel(PUSH2));
  Multiplexer #(.width(32), .enable("false")) multiplexer_9 (
    .in0(multiplexer_8_out), .in1(32'h1), .out(MEMORY_OUT), .sel(PUSH1));
  Shifter #(.width(32)) shifter_1 (.in(out_30), .\dist (5'b00001), .out(shifter_1_out));
  Counter #(.width(32), .max('hffffffff)) counter_1 (
    .count(LCTR), .Q(CTR), .clk(CLK), .clr(CLR));  // open: load, D, carry
  Adder #(.width(32)) adder_4 (.a(shifter_1_out), .b(32'h1), .out(P_2_1), .cout(adder_4_cout));  // open: cin
  Adder #(.width(32)) adder_5 (.a(32'h1), .b(P_2_1), .out(P_2_2), .cin(adder_4_cout));  // open: cout
  Negator #(.width(32)) negator_1 (.in(32'h1), .out(negator_1_out));
  Comparator #(.width(32), .mode("unsigned")) comparator_1 (.a(A), .b(negator_1_out), .eq(A_____1));  // open: gt, lt
  Comparator #(.width(32), .mode("unsigned")) comparator_2 (.a(P_2_1), .b(N), .lt(P_2_1___N));  // open: gt, eq
  Comparator #(.width(32), .mode("unsigned")) comparator_3 (.a(P_2_2), .b(N), .lt(P_2_2___N));  // open: gt, eq
  PRINT_UDEC print_udec_1 (
    .num(CTR), .start(Write), .CLK(CLK), .RST(CLR), .ASCII(ASCII), .Write_ASCII(WASCII));  // open: end

  assign out_31 = F;

  // Other names for the same wires on the sheet: DI[31:0] = DATA_INPUT; DIR[23:0] = DIR_INPUT;
  //   DIRM[23:0] = DIR_MEMORY; MI[31:0] = MEMORY_IN; MO[31:0] = MEMORY_OUT; P[31:0] = out_30; SP[31:0] = out_32;
  //   WriteM = Write_OUTPUT
endmodule

module CONTROL_UNIT (
  input  CLK,
  input  CLR,
  input  Start,
  input  A_____1,
  input  [31:0] F,
  input  P_2_1___N,
  input  P_2_2___N,
  output LN,
  output LP1,
  output LP2,
  output LA,
  output LCTR,
  output LF,
  output RET,
  output INVALID,
  output END,
  output CALL1,
  output CALL2,
  output CALL3,
  output PUSH01,
  output PUSH02,
  output PUSH1,
  output PUSH2,
  output PUSHP1,
  output Write,
  output PUSHP2
);

  wire demultiplexer_1_out0, demultiplexer_2_out0, demultiplexer_3_out2, demultiplexer_4_out1,
       demultiplexer_5_out0, IDLE_q, JMP, or_1_out, WAIT_10_q, WAIT_11_q, WAIT_12_q, WAIT_q;

  D_Flip_Flop IDLE (.clk(CLK), .D(demultiplexer_1_out0), .Q(IDLE_q), .preset(CLR));  // open: Qn, en, reset
  D_Flip_Flop d_ff_1 (.clk(Write), .D(Write), .Q(END), .reset(CLR));  // open: Qn, preset, en
  Demultiplexer #(.enable("false")) demultiplexer_1 (.out0(demultiplexer_1_out0), .out1(LN), .in(IDLE_q), .sel(Start));
  D_Flip_Flop WAIT (.clk(CLK), .D(LP2), .Q(WAIT_q), .reset(CLR));  // open: Qn, preset, en
  Demultiplexer #(.enable("false")) demultiplexer_2 (
    .out0(demultiplexer_2_out0), .out1(PUSH2), .in(WAIT_q), .sel(P_2_2___N));
  D_Flip_Flop WAIT_2 (.clk(CLK), .D(LN), .Q(PUSH01), .reset(CLR));  // open: Qn, preset, en
  D_Flip_Flop WAIT_3 (.clk(CLK), .D(PUSH2), .Q(PUSHP2), .reset(CLR));  // open: Qn, preset, en
  D_Flip_Flop WAIT_4 (.clk(CLK), .D(PUSH01), .Q(PUSH02), .reset(CLR));  // open: Qn, preset, en
  D_Flip_Flop WAIT_5 (.clk(CLK), .D(PUSHP2), .Q(CALL3), .reset(CLR));  // open: Qn, preset, en
  D_Flip_Flop WAIT_6 (.clk(CLK), .D(PUSH02), .Q(CALL1), .reset(CLR));  // open: Qn, preset, en
  or or_1 (or_1_out, CALL1, CALL3, CALL2);
  D_Flip_Flop WAIT_7 (.clk(CLK), .D(or_1_out), .Q(LP1), .reset(CLR));  // open: Qn, preset, en
  or or_2 (JMP, demultiplexer_2_out0, demultiplexer_3_out2);
  Demultiplexer #(.select(2), .disabled(0), .enable("false")) demultiplexer_3 (
    .out0(Write), .out1(LP2), .out2(demultiplexer_3_out2), .out3(INVALID), .in(WAIT_12_q), .sel(F[1:0]));
  D_Flip_Flop WAIT_8 (.clk(CLK), .D(LP1), .Q(LA), .reset(CLR));  // open: Qn, preset, en
  D_Flip_Flop WAIT_9 (.clk(CLK), .D(RET), .Q(LF), .reset(CLR));  // open: Qn, preset, en
  D_Flip_Flop WAIT_10 (.clk(CLK), .D(LF), .Q(WAIT_10_q), .reset(CLR));  // open: Qn, preset, en
  D_Flip_Flop WAIT_11 (.clk(CLK), .D(LA), .Q(WAIT_11_q), .reset(CLR));  // open: Qn, preset, en
  or or_3 (RET, demultiplexer_4_out1, JMP, demultiplexer_5_out0);
  D_Flip_Flop WAIT_12 (.clk(CLK), .D(WAIT_10_q), .Q(WAIT_12_q), .reset(CLR));  // open: Qn, preset, en
  Demultiplexer #(.enable("false")) demultiplexer_4 (
    .out0(LCTR), .out1(demultiplexer_4_out1), .in(WAIT_11_q), .sel(A_____1));
  Demultiplexer #(.enable("false")) demultiplexer_5 (
    .out0(demultiplexer_5_out0), .out1(PUSH1), .in(LCTR), .sel(P_2_1___N));
  D_Flip_Flop WAIT_13 (.clk(CLK), .D(PUSH1), .Q(PUSHP1), .reset(CLR));  // open: Qn, preset, en
  D_Flip_Flop WAIT_14 (.clk(CLK), .D(PUSHP1), .Q(CALL2), .reset(CLR));  // open: Qn, preset, en
endmodule
